# Fritzing sketch air_gap (saved by Fritzing 0.9.3b)
breadboards: 1

parts:
  Q1 = NPN-Transistor [package="TO92 [THT]"]
  R2 = Resistor [tolerance=±5% resistance=1k package=THT]
  Raspberry_Pi_1 = Raspberry Pi 3 [part_number=RPI-3-V1.2]
  LED1 = LED - 3mm [color="White (4500K)" package="3 mm [THT]"]
  R3 = Resistor [tolerance=±5% resistance=470 package="2010 [SMD]"]
  D1 = Zener Diode [part_number=1N4732A breakdown_voltage=3.6V package="Melf DO-213 AB [SMD]"]

nets:
  N1: Q1.B, R2.Pin_1
  N2: Q1.C, D1.anode
  N3: R2.Pin_0, Raspberry_Pi_1.GPIO24
  N4: Raspberry_Pi_1.GPIO18, R3.Pin_0
  N5: Raspberry_Pi_1.5V, D1.cathode
  N6: LED1.anode, R3.Pin_1
